# Fritzing sketch ruleta (saved by Fritzing 0.9.3b)
breadboards: 1

parts:
  part = Arduino Nano (Rev3.0)
  LED1 = LED - 5mm [color="Red (633nm)" package="5 mm [THT]"]
  part_2 = HEF4094 [package="DIP16 [THT]"]
  DFRobot_DFPlayer_Mini1 = DFRobot DFPlayer Mini [part_number=DFR0299]
  LED2 = LED - 5mm [color="Red (633nm)" package="5 mm [THT]"]
  LED3 = LED - 5mm [color="Red (633nm)" package="5 mm [THT]"]
  LED4 = LED - 5mm [color="Red (633nm)" package="5 mm [THT]"]
  LED5 = LED - 5mm [color="Red (633nm)" package="5 mm [THT]"]
  LED6 = LED - 5mm [color="Red (633nm)" package="5 mm [THT]"]
  LED7 = LED - 5mm [color="Red (633nm)" package="5 mm [THT]"]
  LED8 = LED - 5mm [color="Red (633nm)" package="5 mm [THT]"]
  Disco_principal = Rotary Encoder [package=THT]
  Selector_rotativo = Rotary Encoder [package=THT]
  Switch_del_selector = SWITCH-MOMENTARY-2 [package=tactile_switch_tall]
  SP1 = SPEAKER [package=pcb_mount_speaker]

nets:
  GND: part.GND, part_2.Vss, Disco_principal.EncoderPinC, Selector_rotativo.EncoderPinC, Switch_del_selector.1
  N1: part.D8, part_2.OE
  N2: part.D9, part_2.CLOCK
  N3: part.D10, DFRobot_DFPlayer_Mini1.RX
  N4: part.D11/MOSI, DFRobot_DFPlayer_Mini1.TX
  N5: part.D12/MISO, part_2.DATA
  5V: part.5V, part_2.STROBE, part_2.Vdd, DFRobot_DFPlayer_Mini1.VCC
  N6: part.A5, Switch_del_selector.2
  N7: part.A4, Selector_rotativo.EncoderPinB
  N8: part.A3, Selector_rotativo.EncoderPinA
  N9: part.A2, Disco_principal.EncoderPinB
  N10: part.A1, Disco_principal.EncoderPinA
  N11: LED1.cathode, LED2.cathode, LED3.cathode, LED4.cathode, LED5.cathode, LED6.cathode, LED7.cathode, LED8.cathode
  N12: LED1.anode, part_2.Q1
  N13: part_2.Q2, LED2.anode
  N14: part_2.Q3, LED3.anode
  N15: part_2.Q4, LED4.anode
  N16: part_2.Q8, LED8.anode
  N17: part_2.Q7, LED7.anode
  N18: part_2.Q6, LED6.anode
  N19: part_2.Q5, LED5.anode
  N20: DFRobot_DFPlayer_Mini1.SPK_1, SP1.+
  N21: DFRobot_DFPlayer_Mini1.SPK_2, SP1.-

notes:
  x 6 (5 colores y 1 columna de selección)
